# Fritzing sketch NRF24L01KUMANDALIARABA (saved by Fritzing 0.9.4)

parts:
  Parça1 = Arduino Nano (Rev3.0)
  Mod1 = Nano-V3-0-IO-Expansion-Adapter
  L298N1 = L298N DC motor driver
  Parça2 = NRF24L01+ Breakout Board
  VCC2 = Battery block 9V

nets:
  N1: Parça1.D1/TX, Mod1.D1/TX
  N2: Parça1.D0/RX, Mod1.D0/RX
  N3: Parça1.RESET, Mod1.RST
  GND: Parça1.GND, Mod1.GND, L298N1.GND, Parça2.GND, VCC2.-
  N4: Parça1.D2, Mod1.D2, L298N1.IN1
  N5: Parça1.D3, Mod1.D3_PWM, L298N1.ENA
  N6: Parça1.D4, Mod1.D4, L298N1.IN2
  N7: Parça1.D5, Mod1.D5_PWM, L298N1.ENB
  N8: Parça1.D6, Mod1.D6_PWM, L298N1.IN3
  N9: Parça1.D7, Mod1.D7, L298N1.IN4
  N10: Parça1.D8, Mod1.D8
  N11: Parça1.D9, Mod1.D9_PWM, Parça2.CE
  N12: Parça1.D10, Mod1.D10_PWM/SS, Parça2.CS
  N13: Parça1.D11/MOSI, Mod1.D11_PWM/MOSI, Parça2.MOSI
  N14: Parça1.D12/MISO, Mod1.D12/MISO, Parça2.MISO
  VIN: Parça1.VIN, Mod1.VIN
  5V: Parça1.5V, Mod1.VCC, L298N1.5V, Parça2.VCC
  N15: Parça1.A7, Mod1.A7
  N16: Parça1.A6, Mod1.A6
  N17: Parça1.A5, Mod1.A5/SCL
  N18: Parça1.A4, Mod1.A4/SDA
  N19: Parça1.A3, Mod1.A3
  N20: Parça1.A2, Mod1.A2
  N21: Parça1.A1, Mod1.A1
  N22: Parça1.A0, Mod1.A0
  N23: Parça1.AREF, Mod1.AREF
  N24: Parça1.3V3, Mod1.NC
  N25: Parça1.D13/SCK, Mod1.D13/SCK, Parça2.SCK
  N26: L298N1.12V, VCC2.+

notes:
  nrf24L01 BAĞLANTISI
  CE 9
  CSN10
  SCK 13
  MO 11
  MI 12
  VCC 5V
  GND -
  ENA 3
  IN1 2
  IN2 4
  IN3 6
  IN4 7
  ENB 5

custom parts:
  Nano-V3-0-IO-Expansion-Adapter: Nano V3.0 IO Expansion Adapter Shield. Note pcb view has been supressed as not useful. You can drag a Nano over the Nano connectors and it will connect and appear in schematic (although at present due to a bug, routing will not show as complete in breadboard).
  L298N DC motor driver: 2x DC motor driver with 78M05 positive voltage regulator (7..35 V) L298N: max 46 V, 2 A Set 5 V Enable jumper to enable 5 V regultor (needed for the L298N) and +5 V output at screw terminal or supply external +5 V at screw terminal Set ENA and/or ENB to +5 V to enable motor permanently or supply ENA and/or ENB with PWM signal IN1 and IN2 set rotation directory for motor A (OUT1/OUT2) IN2 and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
