# Fritzing sketch nrf24L01kumanda (saved by Fritzing 0.9.4)

parts:
  VCC2 = Battery block 9V  # not connected
  Mod1 = Nano-V3-0-IO-Expansion-Adapter
  Parça1 = Arduino Nano (Rev3.0)
  Parça2 = NRF24L01+ Breakout Board
  Parça5 = Black Joystick KY-023
  Parça6 = Black Joystick KY-023

nets:
  VCC: Mod1.VCC, Parça1.5V, Parça2.VCC, Parça5.+5V, Parça6.+5V
  GND: Mod1.GND, Parça1.GND, Parça2.GND, Parça5.GND, Parça6.GND
  N1: Mod1.A0, Parça1.A0, Parça6.VRx
  N2: Mod1.A1, Parça1.A1, Parça5.VRy
  N3: Mod1.A7, Parça1.A7
  N4: Mod1.D13/SCK, Parça1.D13/SCK, Parça2.SCK
  N5: Mod1.NC, Parça1.3V3
  N6: Mod1.AREF, Parça1.AREF
  N7: Mod1.A2, Parça1.A2
  N8: Mod1.A3, Parça1.A3
  N9: Mod1.A4/SDA, Parça1.A4
  N10: Mod1.A5/SCL, Parça1.A5
  N11: Mod1.A6, Parça1.A6
  N12: Mod1.RST, Parça1.RESET
  VIN: Mod1.VIN, Parça1.VIN
  N13: Mod1.D12/MISO, Parça1.D12/MISO, Parça2.MISO
  N14: Mod1.D11_PWM/MOSI, Parça1.D11/MOSI, Parça2.MOSI
  N15: Mod1.D10_PWM/SS, Parça1.D10, Parça2.CS
  N16: Mod1.D9_PWM, Parça1.D9, Parça2.CE
  N17: Mod1.D8, Parça1.D8
  N18: Mod1.D7, Parça1.D7
  N19: Mod1.D6_PWM, Parça1.D6
  N20: Mod1.D5_PWM, Parça1.D5
  N21: Mod1.D4, Parça1.D4
  N22: Mod1.D3_PWM, Parça1.D3
  N23: Mod1.D2, Parça1.D2
  N24: Mod1.D0/RX#64, Mod1.D1/TX#83, Parça1.D0/RX
  N25: Mod1.D1/TX#65, Mod1.D0/RX#80, Parça1.D1/TX

notes:
  nrf24L01 BAĞLANTISI
  CE 9
  CSN10
  SCK 13
  MO 11
  MI 12
  VCC 5V
  GND - GND

custom parts:
  Nano-V3-0-IO-Expansion-Adapter: Nano V3.0 IO Expansion Adapter Shield. Note pcb view has been supressed as not useful. You can drag a Nano over the Nano connectors and it will connect and appear in schematic (although at present due to a bug, routing will not show as complete in breadboard).
  Black Joystick KY-023: Description: The joystick is a combination of 2 analoog potentiometer and a digital switch. Arduino GND --> Module pin - Arduino +5V --> Module pin +5V Arduino Analoog 0 --> Module VRx Arduino Analoog 1 --> Module VRy Arduino Digital --> Module SW Dimensions: 1" x 1.25"
